# Fritzing sketch one_led_2 (saved by Fritzing 0.9.3b)
breadboards: 2

parts:
  R1 = Resistor [tolerance=±5% resistance=220 package=THT]
  Part1 = Arduino Uno (Rev3) - ICSP
  LED2 = LED - 5mm [color="Red (633nm)" package="5 mm [THT]"]
  LED3 = RGB LED (com. anode, rbg) [package="5 mm [THT]"]
  Part2 = Arduino Uno (Rev3) - ICSP
  R3 = Resistor [tolerance=±5% resistance=220 package=THT]

nets:
  N1: R1.Pin_0, Part1.D8
  N2: R1.Pin_1, LED2.anode
  N3: Part1.GND, LED2.cathode
  N4: LED3.red_cathode, Part2.D8
  N5: LED3.green_cathode, Part2.D9_PWM
  N6: Part2.5V, R3.Pin_0

notes:
  5V
  RED
  BLUE
